# Fritzing sketch Ligação simples arduino - driver - stepper (saved by Fritzing 0.9.6b)

parts:
  Driver1 = 28BYJ-48 Driver Module [part_number=ULN2003 package=THT]
  SM1 = 28BYJ-48 Stepper Motor [part_number=28BYJ-48]  # not connected
  Arduino = Arduino Uno (Rev3)

nets:
  N1: Driver1.IN1, Arduino.A1
  N2: Driver1.IN2, Arduino.A2
  N3: Driver1.IN3, Arduino.A3
  N4: Driver1.IN4, Arduino.A4/SDA
  GND: Driver1.GND, Arduino.GND
  N5: Driver1.Vmotor, Arduino.5V

custom parts:
  28BYJ-48 Driver Module: Generic male header
  28BYJ-48 Stepper Motor: Unipolar Stepper Motor 28BYJ-48 Top coil - pink & orange Bottom coil - blue & yellow Common rail - red Connector pins: blue - pink - yellow - orange - red
